// Logisim project and.circ as structural Verilog: 1 circuit, main circuit implementation
module implementation (
  input  A,
  input  B,
  output Y
);

  wire nand_1_out;

  nand nand_1 (nand_1_out, A, B);
  nand nand_2 (Y, nand_1_out, nand_1_out);
endmodule
