// Logisim project nand.circ as structural Verilog: 1 circuit, main circuit implementation
module implementation (
  input  A,
  input  B,
  output Y
);

  wire pull_resistor_2_node, transistor_2_out;

  Pull_Resistor #(.pull(1)) pull_resistor_1 (.node(Y));
  Transistor #(.\type ("n")) transistor_1 (.in(transistor_2_out), .out(Y), .gate(A));
  Transistor #(.\type ("n")) transistor_2 (.in(pull_resistor_2_node), .out(transistor_2_out), .gate(B));
  Pull_Resistor pull_resistor_2 (.node(pull_resistor_2_node));
endmodule
