// Logisim project xor.circ as structural Verilog: 1 circuit, main circuit implementation
module implementation (
  input  A,
  input  B,
  output Y
);

  wire nand_1_out, nand_2_out, nand_3_out, nand_4_out, nand_5_out, nand_6_out, nand_7_out;

  nand nand_1 (nand_1_out, A, A);
  nand nand_2 (nand_2_out, B, B);
  nand nand_3 (nand_3_out, A, B);
  nand nand_4 (nand_4_out, nand_3_out, nand_3_out);
  nand nand_5 (nand_5_out, nand_1_out, nand_2_out);
  nand nand_6 (nand_6_out, nand_4_out, nand_4_out);
  nand nand_7 (nand_7_out, nand_5_out, nand_6_out);
  nand nand_8 (Y, nand_7_out, nand_7_out);
endmodule
