// Logisim project adder4.circ as structural Verilog: 3 circuits, main circuit main
module main (
  input  [3:0] Aval,
  input  [3:0] Bval,
  input  Cinval,
  output [3:0] Sum,
  output Cout
);

  implementation implementation_1 (.Ain(Aval), .Bin(Bval), .Cinin(Cinval), .Sum_Out(Sum), .Carry_Out(Cout));
endmodule

module full_adder (
  input  Ain,
  input  Bin,
  input  Cinin,
  output Carry_Out,
  output Sum_Out
);

  wire and_1_out, and_2_out, and_3_out, xor_1_out;

  or or_1 (Carry_Out, and_1_out, and_2_out, and_3_out);
  and and_1 (and_1_out, Ain, Bin);
  and and_2 (and_2_out, Ain, Cinin);
  and and_3 (and_3_out, Bin, Cinin);
  xor xor_1 (xor_1_out, Ain, Bin);
  xor xor_2 (Sum_Out, xor_1_out, Cinin);
endmodule

module implementation (
  input  [3:0] Ain,
  input  [3:0] Bin,
  input  Cinin,
  output [3:0] Sum_Out,
  output Carry_Out
);

  wire full_adder_2_carry_out, full_adder_3_carry_out, full_adder_4_carry_out;

  full_adder full_adder_1 (
    .Ain(Ain[3]), .Bin(Bin[3]), .Cinin(full_adder_2_carry_out), .Carry_Out(Carry_Out), .Sum_Out(Sum_Out[3]));
  full_adder full_adder_2 (
    .Ain(Ain[2]), .Bin(Bin[2]), .Cinin(full_adder_3_carry_out), .Carry_Out(full_adder_2_carry_out),
    .Sum_Out(Sum_Out[2]));
  full_adder full_adder_3 (
    .Ain(Ain[1]), .Bin(Bin[1]), .Cinin(full_adder_4_carry_out), .Carry_Out(full_adder_3_carry_out),
    .Sum_Out(Sum_Out[1]));
  full_adder full_adder_4 (
    .Ain(Ain[0]), .Bin(Bin[0]), .Cinin(Cinin), .Carry_Out(full_adder_4_carry_out), .Sum_Out(Sum_Out[0]));
endmodule
