// Logisim project alu.circ as structural Verilog: 2 circuits, main circuit main
module main (
  input  [3:0] ALU_OP_IN,
  input  [3:0] A_In,
  input  [3:0] B_In,
  output [3:0] RESULT_OUT
);

  implementation implementation_1 (.ALU_OP_IN(ALU_OP_IN), .A_In(A_In), .B_In(B_In), .RESULT_OUT(RESULT_OUT));
endmodule

module implementation (
  input  [3:0] ALU_OP_IN,
  input  [3:0] A_In,
  input  [3:0] B_In,
  output [3:0] RESULT_OUT
);

  wire [3:0] adder_1_out, and_1_out, multiplexer_1_out, negator_1_out, not_1_out, or_1_out, subtractor_1_out,
       xor_1_out;

  assign not_1_out = ~A_In;  // NOT_Gate not_1, 4 bits wide
  assign and_1_out = A_In & B_In;  // AND_Gate and_1, 4 bits wide
  assign or_1_out = A_In | B_In;  // OR_Gate or_1, 4 bits wide
  assign xor_1_out = A_In ^ B_In;  // XOR_Gate xor_1, 4 bits wide
  Negator #(.width(4)) negator_1 (.in(A_In), .out(negator_1_out));
  Adder #(.width(4)) adder_1 (.a(A_In), .b(B_In), .out(adder_1_out));  // open: cin, cout
  Subtractor #(.width(4)) subtractor_1 (.a(A_In), .b(B_In), .out(subtractor_1_out));  // open: bin, bout
  Multiplexer #(.enable("false"), .select(3), .width(4)) multiplexer_1 (
    .in0(B_In), .in1(A_In), .in2(and_1_out), .in3(or_1_out), .in4(xor_1_out), .in5(not_1_out),
    .in6(negator_1_out), .in7(adder_1_out), .out(multiplexer_1_out), .sel(ALU_OP_IN[2:0]));
  Multiplexer #(.enable("false"), .width(4)) multiplexer_2 (
    .in0(multiplexer_1_out), .in1(subtractor_1_out), .out(RESULT_OUT), .sel(ALU_OP_IN[3]));
endmodule
