// Logisim project dff.circ as structural Verilog: 2 circuits, main circuit main
module main (
  input  D,
  input  clock,
  output Q
);

  implementation implementation_1 (.D(D), .clock(clock), .Q(Q));  // open: out_4
endmodule

module implementation (
  input  D,
  input  clock,
  output Q,
  output out_4
);

  wire nand_1_out, nand_2_out;

  nand nand_1 (nand_1_out, D, clock);
  nand nand_2 (nand_2_out, nand_1_out, clock);
  nand nand_3 (Q, nand_1_out, out_4);
  nand nand_4 (out_4, Q, nand_2_out);
endmodule
