// Logisim project UpDownCounter.circ as structural Verilog: 2 circuits, main circuit main
module main (
  input  EnableIn,
  input  CountUpIn,
  input  CountDownIn,
  input  clkIn,
  output [2:0] Count
);

  implementation implementation_1 (
    .EnableIn(EnableIn), .CountUpIn(CountUpIn), .CountDownIn(CountDownIn), .clkIn(clkIn), .Count(Count));
endmodule

module implementation (
  input  EnableIn,
  input  CountUpIn,
  input  CountDownIn,
  input  clkIn,
  output [2:0] Count
);

  wire B0_out, B1_out, B2_out, C2_out, D0d_out, D1d_out, D2d_out, DN0_out, DN1_out, DN2_out, DownEn_out,
       multiplexer_1_out, multiplexer_2_out, multiplexer_3_out, multiplexer_4_out, multiplexer_5_out,
       multiplexer_6_out, NOT_B2_out, NOT_CountDown_out, NOT_CountUp_out, NOT_Q1_out, NOT_Q2_out, OVF_out,
       S0_out, S1_out, S2_out, UP0_out, UP1_out, UP2_out, UpEn_out;

  and UpEn (UpEn_out, EnableIn, CountUpIn, NOT_CountDown_out);
  and DownEn (DownEn_out, EnableIn, CountDownIn, NOT_CountUp_out);
  not NOT_CountUp (NOT_CountUp_out, CountUpIn);
  not NOT_CountDown (NOT_CountDown_out, CountDownIn);
  D_Flip_Flop d_ff_1 (.D(multiplexer_2_out), .clk(clkIn), .Q(Count[2]));  // open: Qn, preset, reset
  not NOT_Q2 (NOT_Q2_out, Count[2]);
  xor S2 (S2_out, C2_out, Count[2]);
  Multiplexer #(.enable("false")) multiplexer_1 (
    .in0(Count[2]), .in1(UP2_out), .out(multiplexer_1_out), .sel(UpEn_out));
  Multiplexer #(.enable("false")) multiplexer_2 (
    .in0(multiplexer_1_out), .in1(DN2_out), .out(multiplexer_2_out), .sel(DownEn_out));
  not NOT_B2 (NOT_B2_out, B2_out);
  and B2 (B2_out, NOT_Q2_out, B1_out);
  xor D2d (D2d_out, Count[2], B1_out);
  or UP2 (UP2_out, S2_out, OVF_out);
  D_Flip_Flop d_ff_2 (.D(multiplexer_4_out), .clk(clkIn), .Q(Count[1]));  // open: Qn, preset, reset
  not NOT_Q1 (NOT_Q1_out, Count[1]);
  and DN2 (DN2_out, D2d_out, NOT_B2_out);
  or UP1 (UP1_out, S1_out, OVF_out);
  and C2 (C2_out, Count[0], Count[1]);
  xor S1 (S1_out, Count[0], Count[1]);
  Multiplexer #(.enable("false")) multiplexer_3 (
    .in0(Count[1]), .in1(UP1_out), .out(multiplexer_3_out), .sel(UpEn_out));
  Multiplexer #(.enable("false")) multiplexer_4 (
    .in0(multiplexer_3_out), .in1(DN1_out), .out(multiplexer_4_out), .sel(DownEn_out));
  D_Flip_Flop d_ff_3 (.D(multiplexer_6_out), .clk(clkIn), .Q(Count[0]));  // open: Qn, preset, reset
  and B1 (B1_out, NOT_Q1_out, B0_out);
  xor D1d (D1d_out, Count[1], B0_out);
  and DN1 (DN1_out, D1d_out, NOT_B2_out);
  or UP0 (UP0_out, S0_out, OVF_out);
  and OVF (OVF_out, Count[2], Count[1], Count[0]);
  not S0 (S0_out, Count[0]);
  not B0 (B0_out, Count[0]);
  not D0d (D0d_out, Count[0]);
  and DN0 (DN0_out, D0d_out, NOT_B2_out);
  Multiplexer #(.enable("false")) multiplexer_5 (
    .in0(Count[0]), .in1(UP0_out), .out(multiplexer_5_out), .sel(UpEn_out));
  Multiplexer #(.enable("false")) multiplexer_6 (
    .in0(multiplexer_5_out), .in1(DN0_out), .out(multiplexer_6_out), .sel(DownEn_out));
endmodule
