// Logisim project Vending.circ as structural Verilog: 8 circuits, main circuit main
module main (
);

  implementation implementation_1 ();  // open: EnableIn, QuarterReceived, DimeReceived, NickelReceived, ClkIn, Give_Merch, Give_Dime, Give_Nickel
endmodule

module stateCirc (
  input  clk,
  input  Enable,
  input  S2,
  input  S1,
  input  S0,
  output [2:0] State
);

  wire multiplexer_1_out, multiplexer_2_out, multiplexer_3_out;

  Multiplexer #(.enable("false")) multiplexer_1 (.in0(State[2]), .in1(S2), .out(multiplexer_1_out), .sel(Enable));
  Multiplexer #(.enable("false")) multiplexer_2 (.in0(State[1]), .in1(S1), .out(multiplexer_2_out), .sel(Enable));
  Multiplexer #(.enable("false")) multiplexer_3 (.in0(State[0]), .in1(S0), .out(multiplexer_3_out), .sel(Enable));
  D_Flip_Flop d_ff_1 (.D(multiplexer_1_out), .clk(clk), .Q(State[2]));  // open: Qn, preset, reset
  D_Flip_Flop d_ff_2 (.D(multiplexer_2_out), .clk(clk), .Q(State[1]));  // open: Qn, preset, reset
  D_Flip_Flop d_ff_3 (.D(multiplexer_3_out), .clk(clk), .Q(State[0]));  // open: Qn, preset, reset
endmodule

module S0eqa (
  input  bit0,
  input  bit1,
  input  bit2,
  input  [2:0] state,
  output S0
);

  wire and_1_out, and_2_out, and_3_out, and_4_out, and_5_out, and_6_out, and_7_out, not_1_out, not_2_out,
       not_3_out, not_4_out, not_5_out, not_6_out;

  not not_1 (not_1_out, bit0);
  not not_2 (not_2_out, bit1);
  not not_3 (not_3_out, bit2);
  not not_4 (not_4_out, state[2]);
  not not_5 (not_5_out, state[1]);
  not not_6 (not_6_out, state[0]);
  and and_1 (and_1_out, not_1_out, not_2_out, not_3_out, state[0]);
  and and_2 (and_2_out, not_1_out, not_2_out, bit2, not_6_out);
  and and_3 (and_3_out, bit1, not_4_out, state[0]);
  and and_4 (and_4_out, bit1, bit2, state[0]);
  and and_5 (and_5_out, bit0, not_2_out, not_3_out, not_5_out, not_6_out);
  and and_6 (and_6_out, bit0, bit2, state[0]);
  and and_7 (and_7_out, bit0, bit1, state[0]);
  or or_1 (S0, and_1_out, and_2_out, and_3_out, and_4_out, and_5_out, and_6_out, and_7_out);
endmodule

module S1eqa (
  input  bit0,
  input  bit1,
  input  bit2,
  input  [2:0] state,
  output S1
);

  wire and_1_out, and_2_out, and_3_out, and_4_out, and_5_out, and_6_out, and_7_out, and_8_out, not_1_out,
       not_2_out, not_3_out, not_4_out, not_5_out, not_6_out;

  not not_1 (not_1_out, bit0);
  not not_2 (not_2_out, bit1);
  not not_3 (not_3_out, bit2);
  not not_4 (not_4_out, state[2]);
  not not_5 (not_5_out, state[1]);
  not not_6 (not_6_out, state[0]);
  and and_1 (and_1_out, not_1_out, not_2_out, not_3_out, state[1]);
  and and_2 (and_2_out, not_1_out, not_2_out, bit2, not_4_out, state[0]);
  and and_3 (and_3_out, bit2, state[1], not_6_out);
  and and_4 (and_4_out, not_1_out, bit1, not_3_out, not_4_out);
  and and_5 (and_5_out, bit1, bit2, state[1]);
  and and_6 (and_6_out, bit0, not_2_out, not_3_out, not_5_out, not_6_out);
  and and_7 (and_7_out, bit0, bit2, state[1]);
  and and_8 (and_8_out, bit0, bit1, state[1]);
  or or_1 (S1, and_1_out, and_2_out, and_3_out, and_4_out, and_5_out, and_6_out, and_7_out, and_8_out);
endmodule

module S2eqa (
  input  bit0,
  input  bit1,
  input  bit2,
  input  [2:0] state,
  output S2
);

  wire and_1_out, and_2_out, and_3_out, and_4_out, and_5_out, and_6_out, and_7_out, and_8_out, not_1_out,
       not_2_out, not_3_out, not_4_out, not_5_out, not_6_out;

  not not_1 (not_1_out, bit0);
  not not_2 (not_2_out, bit1);
  not not_3 (not_3_out, bit2);
  not not_4 (not_4_out, state[2]);
  not not_5 (not_5_out, state[1]);
  not not_6 (not_6_out, state[0]);
  and and_1 (and_1_out, not_1_out, not_2_out, not_3_out, state[2]);
  and and_2 (and_2_out, not_1_out, not_2_out, bit2, not_4_out, state[1], state[0]);
  and and_3 (and_3_out, bit2, state[2], not_6_out);
  and and_4 (and_4_out, not_1_out, bit1, not_3_out, not_4_out, state[1]);
  and and_5 (and_5_out, bit1, bit2, state[2]);
  and and_6 (and_6_out, bit0, not_2_out, not_3_out, not_5_out, not_6_out);
  and and_7 (and_7_out, bit0, bit2, state[2]);
  and and_8 (and_8_out, bit0, bit1, state[2]);
  or or_1 (S2, and_1_out, and_2_out, and_3_out, and_4_out, and_5_out, and_6_out, and_7_out, and_8_out);
endmodule

module nextState (
  input  bit0,
  input  bit1,
  input  bit2,
  input  [2:0] state,
  output [2:0] stateOut
);

  S0eqa s0eqa_1 (.bit0(bit0), .bit1(bit1), .bit2(bit2), .state(state), .S0(stateOut[0]));
  S1eqa s1eqa_1 (.bit0(bit0), .bit1(bit1), .bit2(bit2), .state(state), .S1(stateOut[1]));
  S2eqa s2eqa_1 (.bit0(bit0), .bit1(bit1), .bit2(bit2), .state(state), .S2(stateOut[2]));
endmodule

module outputCirc (
  input  bit0,
  input  bit1,
  input  bit2,
  input  [2:0] state,
  output [2:0] merch
);

  wire and_1_out, and_2_out, and_3_out, and_4_out, and_5_out, and_6_out, and_7_out, and_8_out, and_9_out,
       not_1_out, not_2_out, not_3_out;

  not not_1 (not_1_out, bit1);
  not not_2 (not_2_out, bit2);
  not not_3 (not_3_out, state[0]);
  and and_1 (and_1_out, bit2, state[2], state[0]);
  and and_2 (and_2_out, bit1, state[2]);
  and and_3 (and_3_out, bit0, state[0]);
  and and_4 (and_4_out, bit0, state[1]);
  and and_5 (and_5_out, bit0, state[1], state[0]);
  and and_6 (and_6_out, bit0, state[2]);
  and and_7 (and_7_out, bit1, state[2], state[0]);
  and and_8 (and_8_out, bit0, not_1_out, not_2_out, state[1], not_3_out);
  and and_9 (and_9_out, bit0, state[2]);
  or or_1 (merch[2], and_1_out, and_2_out, and_3_out, and_4_out);
  or or_2 (merch[1], and_5_out, and_6_out);
  or or_3 (merch[0], and_7_out, and_8_out, and_9_out);
endmodule

module implementation (
  input  EnableIn,
  input  QuarterReceived,
  input  DimeReceived,
  input  NickelReceived,
  input  ClkIn,
  output Give_Merch,
  output Give_Dime,
  output Give_Nickel
);

  wire [2:0] currentState, nextstate_1_stateout;

  nextState nextstate_1 (
    .bit0(QuarterReceived), .bit1(DimeReceived), .bit2(NickelReceived), .state(currentState),
    .stateOut(nextstate_1_stateout));
  outputCirc outputcirc_1 (
    .bit0(QuarterReceived), .bit1(DimeReceived), .bit2(NickelReceived), .state(currentState),
    .merch({Give_Merch, Give_Dime, Give_Nickel}));
  stateCirc statecirc_1 (
    .clk(ClkIn), .Enable(EnableIn), .S2(nextstate_1_stateout[2]), .S1(nextstate_1_stateout[1]),
    .S0(nextstate_1_stateout[0]), .State(currentState));
endmodule
