// Logisim project CPU.circ as structural Verilog: 24 circuits, main circuit implementation
module alu (
  input  [7:0] A,
  input  [7:0] B,
  input  ALU_0,
  input  ALU1,
  output [7:0] out_5
);

  wire [7:0] adder_1_out, multiplier_1_out, nand_1_out, subtractor_1_out;

  Adder adder_1 (.a(A), .b(B), .out(adder_1_out));  // open: cin, cout
  Subtractor subtractor_1 (.a(A), .b(B), .out(subtractor_1_out));  // open: bin, bout
  Multiplier multiplier_1 (.a(A), .b(B), .out(multiplier_1_out));  // open: cin, cout
  assign nand_1_out = ~(A & B);  // NAND_Gate nand_1, 8 bits wide
  Multiplexer #(.enable("false"), .select(2), .width(8)) multiplexer_1 (
    .in0(nand_1_out), .in1(multiplier_1_out), .in2(subtractor_1_out), .in3(adder_1_out), .out(out_5),
    .sel({ALU_0, ALU1}));
endmodule

module implementation (
  output [7:0] print_R0,
  output [7:0] print_R1,
  output halt
);

  wire ALU_0, ALU_1, and_1_out, and_2_out, and_3_out, and_4_out, and_5_out, and_6_out, and_7_out, and_9_out,
       and_10_out, BUSS, clk, comparator_1_eq, comparator_2_eq, IR_IN, IR_OUT, M_READ, M_WRITE, MAR_IN,
       MDR_IN, MDR_OUT, NOT_I2_out, NOT_I3_out, OFFSET, ONE_OUT, or_1_out, or_2_out, or_3_out, or_4_out,
       or_5_out, PC_IN, PC_OUT, RDS_IN, RDS_OUT, RS_IN, RS_OUT, X_IN, Z_IN, Z_OUT;
  wire [2:0] controlled_buffer_3_out;
  wire [4:0] state, state_m_1_next_state;
  wire [7:0] alu_1_out_5, bit_extender_1_out, controlled_buffer_1_out, controlled_buffer_2_out,
       controlled_buffer_5_out, IR, MAR_q, MDR_q, multiplexer_1_out, PC, ram_1_dout, X_q, Z_q;
  wire [7:3] controlled_buffer_3_out_2;

  Clock clock_1 (.out(clk));
  or or_1 (or_1_out, MDR_IN, M_READ);
  assign controlled_buffer_1_out = MDR_IN ? {controlled_buffer_3_out_2, controlled_buffer_3_out} : 8'bz;  // Controlled_Buffer controlled_buffer_1
  Register #(.trigger("high")) MDR (.D(controlled_buffer_1_out), .en(or_1_out), .clk(clk), .Q(MDR_q));  // open: clr
  assign controlled_buffer_2_out = M_WRITE ? MDR_q : 8'bz;  // Controlled_Buffer controlled_buffer_2
  RAM ram_1 (.addr(MAR_q), .we(M_WRITE), .oe(M_READ), .clk(clk), .din(controlled_buffer_2_out), .dout(ram_1_dout));
  Register u_PC (.D({controlled_buffer_3_out_2, controlled_buffer_3_out}), .en(PC_IN), .clk(clk), .Q(PC));  // open: clr
  assign {controlled_buffer_3_out_2, controlled_buffer_3_out} = MDR_OUT ? MDR_q : 8'bz;  // Controlled_Buffer controlled_buffer_3
  not NOT_I3 (NOT_I3_out, IR[3]);
  not NOT_I2 (NOT_I2_out, IR[2]);
  assign {controlled_buffer_3_out_2, controlled_buffer_3_out} = PC_OUT ? PC : 8'bz;  // Controlled_Buffer controlled_buffer_4
  assign controlled_buffer_5_out = MAR_IN ? {controlled_buffer_3_out_2, controlled_buffer_3_out} : 8'bz;  // Controlled_Buffer controlled_buffer_5
  Register MAR (.D(controlled_buffer_5_out), .en(MAR_IN), .clk(clk), .Q(MAR_q));  // open: clr
  state_m state_m_1 (.current_state(state), .opcode(IR[7:4]), .next_state(state_m_1_next_state));
  pcOut pcout_1 (.state(state), .pc_out(PC_OUT));
  marIn marin_1 (.state(state), .mar_in(MAR_IN));
  mRead mread_1 (.state(state), .m_read(M_READ));
  xIn xin_1 (.state(state), .x_in(X_IN));
  zIn zin_1 (.state(state), .z_in(Z_IN));
  oneOut oneout_1 (.state(state), .one_out(ONE_OUT));
  pcIn pcin_1 (.state(state), .pc_in(PC_IN));
  aluZero aluzero_1 (.state(state), .alu_zero(ALU_0));
  aluOne aluone_1 (.state(state), .alu_one(ALU_1));
  busss busss_1 (.state(state), .buss(BUSS));
  zOut zout_1 (.state(state), .z_out(Z_OUT));
  mdrOut mdrout_1 (.state(state), .mdr_out(MDR_OUT));
  irIn irin_1 (.state(state), .ir_in(IR_IN));
  rdsOut rdsout_1 (.state(state), .rds_out(RDS_OUT));
  rsOut rsout_1 (.state(state), .rs_out(RS_OUT));
  rdsIn rdsin_1 (.state(state), .rds_in(RDS_IN));
  irOut irout_1 (.state(state), .ir_out(IR_OUT));
  offset_val offset_val_1 (.state(state), .offset(OFFSET));
  mdrIn mdrin_1 (.state(state), .mdr_in(MDR_IN));
  mWrite mwrite_1 (.state(state), .m_write(M_WRITE));
  rsIn rsin_1 (.state(state), .rs_in(RS_IN));
  assign controlled_buffer_1_out = M_READ ? ram_1_dout : 8'bz;  // Controlled_Buffer controlled_buffer_6
  Register #(.width(5)) register_1 (.D(state_m_1_next_state), .en(1'b1), .clk(clk), .Q(state));  // open: clr
  and and_1 (and_1_out, NOT_I3_out, RDS_IN);
  and and_2 (and_2_out, NOT_I2_out, RS_IN);
  or or_2 (or_2_out, and_1_out, and_2_out);
  Register #(.trigger("high")) u_IR (
    .D({controlled_buffer_3_out_2, controlled_buffer_3_out}), .en(IR_IN), .clk(clk), .Q(IR));  // open: clr
  assign {controlled_buffer_3_out_2, controlled_buffer_3_out} = IR_OUT ? IR : 8'bz;  // Controlled_Buffer controlled_buffer_7
  and and_3 (and_3_out, NOT_I3_out, RDS_OUT);
  and and_4 (and_4_out, NOT_I2_out, RS_OUT);
  or or_3 (or_3_out, and_3_out, and_4_out);
  Register R0 (
    .D({controlled_buffer_3_out_2, controlled_buffer_3_out}), .en(or_2_out), .clk(clk), .Q(print_R0));  // open: clr
  assign {controlled_buffer_3_out_2, controlled_buffer_3_out} = or_3_out ? print_R0 : 8'bz;  // Controlled_Buffer controlled_buffer_8
  and and_5 (and_5_out, controlled_buffer_3_out_2[3], OFFSET);
  and and_6 (and_6_out, IR[3], RDS_IN);
  or or_4 (or_4_out, and_6_out, and_7_out);
  assign bit_extender_1_out = {{5{and_5_out}}, controlled_buffer_3_out};  // Bit_Extender bit_extender_1
  Comparator comparator_1 (.a(PC), .b(8'hf), .eq(comparator_1_eq));  // open: gt, lt
  Comparator comparator_2 (.a(IR), .b({8{1'b0}}), .eq(comparator_2_eq));  // open: gt, lt
  and and_7 (and_7_out, IR[2], RS_IN);
  Register R1 (
    .D({controlled_buffer_3_out_2, controlled_buffer_3_out}), .en(or_4_out), .clk(clk), .Q(print_R1));  // open: clr
  Multiplexer #(.enable("false"), .width(8)) multiplexer_1 (
    .in0(bit_extender_1_out), .in1({controlled_buffer_3_out_2, controlled_buffer_3_out}),
    .out(multiplexer_1_out), .sel(BUSS));
  and and_8 (halt, comparator_1_eq, comparator_2_eq);
  and and_9 (and_9_out, IR[3], RDS_OUT);
  or or_5 (or_5_out, and_9_out, and_10_out);
  assign {controlled_buffer_3_out_2, controlled_buffer_3_out} = or_5_out ? print_R1 : 8'bz;  // Controlled_Buffer controlled_buffer_9
  Register X (.D({controlled_buffer_3_out_2, controlled_buffer_3_out}), .en(X_IN), .clk(clk), .Q(X_q));  // open: clr
  alu u_alu_1 (.A(multiplexer_1_out), .B(X_q), .ALU_0(ALU_0), .ALU1(ALU_1), .out_5(alu_1_out_5));
  and and_10 (and_10_out, IR[2], RS_OUT);
  Register Z (.D(alu_1_out_5), .en(Z_IN), .clk(clk), .Q(Z_q));  // open: clr
  assign {controlled_buffer_3_out_2, controlled_buffer_3_out} = ONE_OUT ? 8'h1 : 8'bz;  // Controlled_Buffer controlled_buffer_10
  assign {controlled_buffer_3_out_2, controlled_buffer_3_out} = Z_OUT ? Z_q : 8'bz;  // Controlled_Buffer controlled_buffer_11

  // Other names for the same wires on the sheet: opcode[3:0] = IR[7:4]; R0[7:0] = print_R0; R1[7:0] = print_R1
endmodule

module state_m (
  input  [4:0] current_state,
  input  [3:0] opcode,
  output [4:0] next_state
);

  wire and_1_out, and_2_out, and_3_out, and_4_out, and_5_out, and_6_out, and_7_out, and_8_out, and_9_out,
       and_10_out, and_11_out, and_12_out, and_13_out, and_14_out, and_15_out, and_16_out, and_17_out,
       and_18_out, and_19_out, and_20_out, and_21_out, and_22_out, and_23_out, and_24_out, and_25_out,
       not_1_out, not_2_out, not_3_out, not_4_out, not_5_out, not_6_out, not_7_out, not_8_out;

  not not_1 (not_1_out, current_state[4]);
  not not_2 (not_2_out, current_state[3]);
  not not_3 (not_3_out, current_state[2]);
  not not_4 (not_4_out, current_state[1]);
  not not_5 (not_5_out, current_state[0]);
  not not_6 (not_6_out, opcode[3]);
  not not_7 (not_7_out, opcode[2]);
  not not_8 (not_8_out, opcode[1]);
  and and_1 (and_1_out, not_1_out, not_2_out, not_3_out, current_state[1], current_state[0], opcode[2]);
  and and_2 (and_2_out, current_state[3], current_state[2], current_state[1], current_state[0]);
  and and_3 (and_3_out, current_state[4], not_4_out, current_state[0]);
  and and_4 (and_4_out, current_state[4], not_3_out, current_state[1], not_5_out);
  and and_5 (and_5_out, current_state[4], current_state[2], not_4_out);
  and and_6 (and_6_out, not_1_out, not_2_out, current_state[1], current_state[0], not_6_out, opcode[1]);
  and and_7 (and_7_out, not_2_out, current_state[2], current_state[1], current_state[0]);
  and and_8 (and_8_out, current_state[3], not_5_out);
  and and_9 (and_9_out, current_state[3], not_3_out, current_state[1]);
  and and_10 (and_10_out, not_1_out, not_3_out, current_state[1], current_state[0], not_7_out, not_8_out);
  and and_11 (and_11_out, not_1_out, not_3_out, current_state[1], current_state[0], opcode[0]);
  and and_12 (and_12_out, not_2_out, current_state[2], not_4_out);
  and and_13 (and_13_out, current_state[3], not_3_out, current_state[1], current_state[0]);
  and and_14 (and_14_out, current_state[3], current_state[2], not_5_out);
  and and_15 (and_15_out, not_2_out, not_4_out, current_state[0]);
  and and_16 (and_16_out, not_3_out, current_state[1], not_5_out);
  and and_17 (and_17_out, not_1_out, not_2_out, not_3_out, current_state[1], not_6_out, opcode[0]);
  and and_18 (and_18_out, not_1_out, not_2_out, not_3_out, current_state[1], not_6_out, opcode[1]);
  and and_19 (and_19_out, current_state[3], current_state[1], not_5_out);
  and and_20 (and_20_out, not_1_out, not_4_out, not_5_out);
  and and_21 (and_21_out, not_3_out, current_state[1], not_5_out);
  and and_22 (and_22_out, not_1_out, not_2_out, not_3_out, current_state[1], not_8_out, opcode[0]);
  and and_23 (and_23_out, not_1_out, not_2_out, not_3_out, current_state[1], not_6_out, opcode[2]);
  and and_24 (and_24_out, current_state[2], not_4_out, not_5_out);
  and and_25 (and_25_out, current_state[3], not_5_out);
  or or_1 (next_state[4], and_1_out, and_2_out, and_3_out, and_4_out, and_5_out);
  or or_2 (next_state[3], and_6_out, and_7_out, and_8_out, and_9_out);
  or or_3 (next_state[2], and_10_out, and_11_out, and_12_out, and_13_out, and_14_out);
  or or_4 (next_state[1], and_15_out, and_16_out, and_17_out, and_18_out, and_19_out);
  or or_5 (next_state[0], and_20_out, and_21_out, and_22_out, and_23_out, and_24_out, and_25_out);
endmodule

module pcOut (
  input  [4:0] state,
  output pc_out
);

  wire and_1_out, and_2_out, not_1_out, not_2_out, not_3_out, not_4_out, not_5_out;

  not not_1 (not_1_out, state[4]);
  not not_2 (not_2_out, state[3]);
  not not_3 (not_3_out, state[2]);
  not not_4 (not_4_out, state[1]);
  not not_5 (not_5_out, state[0]);
  and and_1 (and_1_out, not_1_out, not_2_out, not_3_out, not_4_out, not_5_out);
  and and_2 (and_2_out, state[4], not_2_out, state[2], not_4_out, not_5_out);
  or or_1 (pc_out, and_1_out, and_2_out);
endmodule

module marIn (
  input  [4:0] state,
  output mar_in
);

  wire and_1_out, and_2_out, not_1_out, not_2_out, not_3_out, not_4_out, not_5_out;

  not not_1 (not_1_out, state[4]);
  not not_2 (not_2_out, state[3]);
  not not_3 (not_3_out, state[2]);
  not not_4 (not_4_out, state[1]);
  not not_5 (not_5_out, state[0]);
  and and_1 (and_1_out, not_1_out, not_2_out, not_3_out, not_4_out, not_5_out);
  and and_2 (and_2_out, not_1_out, state[3], not_3_out, state[1], not_5_out);
  or or_1 (mar_in, and_1_out, and_2_out);
endmodule

module mRead (
  input  [4:0] state,
  output m_read
);

  wire and_1_out, and_2_out, and_3_out, not_1_out, not_2_out, not_3_out, not_4_out, not_5_out;

  not not_1 (not_1_out, state[4]);
  not not_2 (not_2_out, state[3]);
  not not_3 (not_3_out, state[2]);
  not not_4 (not_4_out, state[1]);
  not not_5 (not_5_out, state[0]);
  and and_1 (and_1_out, not_1_out, not_2_out, not_3_out, not_4_out);
  and and_2 (and_2_out, not_1_out, not_2_out, not_3_out, not_5_out);
  and and_3 (and_3_out, not_1_out, state[3], not_3_out, state[1]);
  or or_1 (m_read, and_1_out, and_2_out, and_3_out);
endmodule

module xIn (
  input  [4:0] state,
  output x_in
);

  wire and_1_out, and_2_out, and_3_out, and_4_out, and_5_out, and_6_out, not_1_out, not_2_out, not_3_out,
       not_4_out, not_5_out;

  not not_1 (not_1_out, state[4]);
  not not_2 (not_2_out, state[3]);
  not not_3 (not_3_out, state[2]);
  not not_4 (not_4_out, state[1]);
  not not_5 (not_5_out, state[0]);
  and and_1 (and_1_out, not_1_out, not_2_out, not_4_out, not_5_out);
  and and_2 (and_2_out, not_2_out, state[2], not_4_out, not_5_out);
  and and_3 (and_3_out, not_1_out, not_2_out, state[2], state[1], state[0]);
  and and_4 (and_4_out, not_1_out, state[3], not_3_out, state[1], state[0]);
  and and_5 (and_5_out, not_1_out, state[3], state[2], state[1], not_5_out);
  and and_6 (and_6_out, state[4], not_2_out, not_3_out, not_4_out, state[0]);
  or or_1 (x_in, and_1_out, and_2_out, and_3_out, and_4_out, and_5_out, and_6_out);
endmodule

module zIn (
  input  [4:0] state,
  output z_in
);

  wire and_1_out, and_2_out, and_3_out, and_4_out, and_5_out, not_1_out, not_2_out, not_3_out, not_4_out,
       not_5_out;

  not not_1 (not_1_out, state[4]);
  not not_2 (not_2_out, state[3]);
  not not_3 (not_3_out, state[2]);
  not not_4 (not_4_out, state[1]);
  not not_5 (not_5_out, state[0]);
  and and_1 (and_1_out, not_1_out, not_2_out, not_4_out, state[0]);
  and and_2 (and_2_out, not_2_out, state[2], not_4_out, state[0]);
  and and_3 (and_3_out, not_1_out, state[3], not_4_out, not_5_out);
  and and_4 (and_4_out, not_1_out, state[3], state[2], state[1], state[0]);
  and and_5 (and_5_out, state[4], not_2_out, not_3_out, state[1], not_5_out);
  or or_1 (z_in, and_1_out, and_2_out, and_3_out, and_4_out, and_5_out);
endmodule

module oneOut (
  input  [4:0] state,
  output one_out
);

  wire not_1_out, not_2_out, not_3_out, not_4_out;

  not not_1 (not_1_out, state[4]);
  not not_2 (not_2_out, state[3]);
  not not_3 (not_3_out, state[2]);
  not not_4 (not_4_out, state[1]);
  and and_1 (one_out, not_1_out, not_2_out, not_3_out, not_4_out, state[0]);
endmodule

module pcIn (
  input  [4:0] state,
  output pc_in
);

  wire and_1_out, and_2_out, not_1_out, not_2_out, not_3_out, not_4_out;

  not not_1 (not_1_out, state[4]);
  not not_2 (not_2_out, state[3]);
  not not_3 (not_3_out, state[2]);
  not not_4 (not_4_out, state[0]);
  and and_1 (and_1_out, not_1_out, not_2_out, not_3_out, state[1], not_4_out);
  and and_2 (and_2_out, state[4], not_2_out, state[2], state[1], not_4_out);
  or or_1 (pc_in, and_1_out, and_2_out);
endmodule

module aluZero (
  input  [4:0] state,
  output alu_zero
);

  wire and_1_out, and_2_out, and_3_out, and_4_out, and_5_out, not_1_out, not_2_out, not_3_out, not_4_out,
       not_5_out;

  not not_1 (not_1_out, state[4]);
  not not_2 (not_2_out, state[3]);
  not not_3 (not_3_out, state[2]);
  not not_4 (not_4_out, state[1]);
  not not_5 (not_5_out, state[0]);
  and and_1 (and_1_out, not_1_out, not_2_out, not_3_out, not_4_out, state[0]);
  and and_2 (and_2_out, not_1_out, state[3], not_4_out, not_5_out);
  and and_3 (and_3_out, not_1_out, state[3], state[2], state[1], state[0]);
  and and_4 (and_4_out, state[4], not_2_out, not_3_out, state[1], not_5_out);
  and and_5 (and_5_out, state[4], not_2_out, state[2], not_4_out, state[0]);
  or or_1 (alu_zero, and_1_out, and_2_out, and_3_out, and_4_out, and_5_out);
endmodule

module aluOne (
  input  [4:0] state,
  output alu_one
);

  wire and_1_out, and_2_out, and_3_out, and_4_out, not_1_out, not_2_out, not_3_out, not_4_out, not_5_out;

  not not_1 (not_1_out, state[4]);
  not not_2 (not_2_out, state[3]);
  not not_3 (not_3_out, state[2]);
  not not_4 (not_4_out, state[1]);
  not not_5 (not_5_out, state[0]);
  and and_1 (and_1_out, not_1_out, not_2_out, not_3_out, not_4_out, state[0]);
  and and_2 (and_2_out, not_1_out, state[3], not_4_out, not_5_out);
  and and_3 (and_3_out, not_1_out, state[3], state[2], state[1], state[0]);
  and and_4 (and_4_out, state[4], not_2_out, state[2], not_4_out, state[0]);
  or or_1 (alu_one, and_1_out, and_2_out, and_3_out, and_4_out);
endmodule

module busss (
  input  [4:0] state,
  output buss
);

  wire and_1_out, and_2_out, and_3_out, not_1_out, not_2_out, not_3_out, not_4_out, not_5_out;

  not not_1 (not_1_out, state[4]);
  not not_2 (not_2_out, state[3]);
  not not_3 (not_3_out, state[2]);
  not not_4 (not_4_out, state[1]);
  not not_5 (not_5_out, state[0]);
  and and_1 (and_1_out, not_1_out, not_2_out, not_4_out, state[0]);
  and and_2 (and_2_out, not_1_out, state[3], not_4_out, not_5_out);
  and and_3 (and_3_out, state[4], not_2_out, not_3_out, state[1], not_5_out);
  or or_1 (buss, and_1_out, and_2_out, and_3_out);
endmodule

module zOut (
  input  [4:0] state,
  output z_out
);

  wire and_1_out, and_2_out, and_3_out, and_4_out, and_5_out, not_1_out, not_2_out, not_3_out, not_4_out,
       not_5_out;

  not not_1 (not_1_out, state[4]);
  not not_2 (not_2_out, state[3]);
  not not_3 (not_3_out, state[2]);
  not not_4 (not_4_out, state[1]);
  not not_5 (not_5_out, state[0]);
  and and_1 (and_1_out, not_1_out, not_2_out, state[1], not_5_out);
  and and_2 (and_2_out, not_2_out, state[2], state[1], not_5_out);
  and and_3 (and_3_out, not_1_out, state[3], not_4_out, state[0]);
  and and_4 (and_4_out, state[4], not_2_out, not_3_out, not_4_out, not_5_out);
  and and_5 (and_5_out, state[4], not_2_out, not_3_out, state[1], state[0]);
  or or_1 (z_out, and_1_out, and_2_out, and_3_out, and_4_out, and_5_out);
endmodule

module mdrOut (
  input  [4:0] state,
  output mdr_out
);

  wire and_1_out, and_2_out, not_1_out, not_2_out, not_3_out, not_4_out, not_5_out;

  not not_1 (not_1_out, state[4]);
  not not_2 (not_2_out, state[3]);
  not not_3 (not_3_out, state[2]);
  not not_4 (not_4_out, state[1]);
  not not_5 (not_5_out, state[0]);
  and and_1 (and_1_out, not_1_out, not_2_out, not_3_out, state[1], state[0]);
  and and_2 (and_2_out, not_1_out, state[3], state[2], not_4_out, not_5_out);
  or or_1 (mdr_out, and_1_out, and_2_out);
endmodule

module irIn (
  input  [4:0] state,
  output ir_in
);

  wire not_1_out, not_2_out, not_3_out;

  not not_1 (not_1_out, state[4]);
  not not_2 (not_2_out, state[3]);
  not not_3 (not_3_out, state[2]);
  and and_1 (ir_in, not_1_out, not_2_out, not_3_out, state[1], state[0]);
endmodule

module rdsOut (
  input  [4:0] state,
  output rds_out
);

  wire and_1_out, and_2_out, and_3_out, and_4_out, and_5_out, not_1_out, not_2_out, not_3_out, not_4_out,
       not_5_out;

  not not_1 (not_1_out, state[4]);
  not not_2 (not_2_out, state[3]);
  not not_3 (not_3_out, state[2]);
  not not_4 (not_4_out, state[1]);
  not not_5 (not_5_out, state[0]);
  and and_1 (and_1_out, not_1_out, not_2_out, state[2], not_4_out, not_5_out);
  and and_2 (and_2_out, not_1_out, not_2_out, state[2], state[1], state[0]);
  and and_3 (and_3_out, not_1_out, state[3], not_3_out, state[1], state[0]);
  and and_4 (and_4_out, not_1_out, state[3], state[2], state[1], not_5_out);
  and and_5 (and_5_out, state[4], not_2_out, not_3_out, state[1], not_5_out);
  or or_1 (rds_out, and_1_out, and_2_out, and_3_out, and_4_out, and_5_out);
endmodule

module rsOut (
  input  [4:0] state,
  output rs_out
);

  wire and_1_out, and_2_out, and_3_out, not_1_out, not_2_out, not_3_out, not_4_out, not_5_out;

  not not_1 (not_1_out, state[4]);
  not not_2 (not_2_out, state[3]);
  not not_3 (not_3_out, state[2]);
  not not_4 (not_4_out, state[1]);
  not not_5 (not_5_out, state[0]);
  and and_1 (and_1_out, not_1_out, not_2_out, state[2], not_4_out, state[0]);
  and and_2 (and_2_out, not_1_out, state[3], not_3_out, not_5_out);
  and and_3 (and_3_out, state[4], not_2_out, not_3_out, not_4_out, state[0]);
  or or_1 (rs_out, and_1_out, and_2_out, and_3_out);
endmodule

module rdsIn (
  input  [4:0] state,
  output rds_in
);

  wire and_1_out, and_2_out, and_3_out, and_4_out, not_1_out, not_2_out, not_3_out, not_4_out, not_5_out;

  not not_1 (not_1_out, state[4]);
  not not_2 (not_2_out, state[3]);
  not not_3 (not_3_out, state[2]);
  not not_4 (not_4_out, state[1]);
  not not_5 (not_5_out, state[0]);
  and and_1 (and_1_out, not_1_out, not_2_out, state[2], state[1], not_5_out);
  and and_2 (and_2_out, not_1_out, state[3], not_4_out, state[0]);
  and and_3 (and_3_out, state[4], not_2_out, not_3_out, not_4_out, not_5_out);
  and and_4 (and_4_out, state[4], not_2_out, not_3_out, state[1], state[0]);
  or or_1 (rds_in, and_1_out, and_2_out, and_3_out, and_4_out);
endmodule

module irOut (
  input  [4:0] state,
  output ir_out
);

  wire and_1_out, and_2_out, not_1_out, not_2_out, not_3_out;

  not not_1 (not_1_out, state[4]);
  not not_2 (not_2_out, state[3]);
  not not_3 (not_3_out, state[1]);
  and and_1 (and_1_out, not_1_out, state[3], state[2], state[1], state[0]);
  and and_2 (and_2_out, state[4], not_2_out, state[2], not_3_out, state[0]);
  or or_1 (ir_out, and_1_out, and_2_out);
endmodule

module offset_val (
  input  [4:0] state,
  output offset
);

  wire not_1_out, not_2_out;

  not not_1 (not_1_out, state[3]);
  not not_2 (not_2_out, state[1]);
  and and_1 (offset, state[4], not_1_out, state[2], not_2_out, state[0]);
endmodule

module mdrIn (
  input  [4:0] state,
  output mdr_in
);


  assign mdr_in = 1'b0;
endmodule

module mWrite (
  input  [4:0] state,
  output m_write
);


  assign m_write = 1'b0;
endmodule

module rsIn (
  input  [4:0] state,
  output rs_in
);


  assign rs_in = 1'b0;
endmodule
